# Fritzing sketch infoscreen (saved by Fritzing 0.9.4)

parts:
  Raspberry_Pi_1 = Raspberry Pi 3 [part_number=RPI-3-V1.2]
  Part1 = BME280 Breakout
  PIR1 = PIR sensor
  S1 = Momentary Switch [package=ksa_sealed_tac_switch]
  S2 = Momentary Switch [package=ksa_sealed_tac_switch]

nets:
  3V3: Raspberry_Pi_1.3v3, Raspberry_Pi_1.3V3, Part1.3.3V, Part1.!CS, PIR1.VDD
  N1: Raspberry_Pi_1.GPIO2, Part1.SDI/SDA
  N2: Raspberry_Pi_1.GPIO3, Part1.SCK/SCL
  N3: Raspberry_Pi_1.GIPO4, PIR1.SIG
  N4: Raspberry_Pi_1.GIPO17, S1.4
  N5: Raspberry_Pi_1.GIPO27, S2.4
  GND: Raspberry_Pi_1.GND, Part1.GND, Part1.SDO/ADR, PIR1.GND
  N6: S1.2, S2.2
